# Fritzing sketch 4-bit Adder (saved by Fritzing 0.9.1b)
breadboards: 1

parts:
  SW1 = DIP Switch 8 Position [package=dipswitch-08]
  7486_XOR1 = IC 7486 Quad XOR Gate [package="DIP (Dual Inline) [THT]"]
  7408_AND1 = IC 7408 AND Gate [package="DIP (Dual Inline) [THT]"]
  7432 = 7432 Quad OR Gate [package="DIP (Dual Inline) [THT]"]
  7486_XOR2 = IC 7486 Quad XOR Gate [package="DIP (Dual Inline) [THT]"]
  7408_AND2 = IC 7408 AND Gate [package="DIP (Dual Inline) [THT]"]

nets:
  N1: SW1.9, 7486_XOR2.XOR_2_-_IN_2, 7408_AND2.AND_2_-_IN_2
  N2: SW1.10, 7486_XOR1.XOR_4_-_IN_2, 7408_AND1.AND_4_-_IN_2
  N3: SW1.11, 7486_XOR1.XOR_2_-_IN_2, 7408_AND1.AND_2_-_IN_2
  N4: SW1.12, 7486_XOR1.XOR_1_-_IN_2, 7408_AND1.AND_1_-_IN_2
  N5: SW1.13, 7486_XOR2.XOR_2_-_IN_1, 7408_AND2.AND_2_-_IN_1
  N6: SW1.14, 7486_XOR1.XOR_4_-_IN_1, 7408_AND1.AND_4_-_IN_1
  N7: SW1.15, 7486_XOR1.XOR_2_-_IN_1, 7408_AND1.AND_2_-_IN_1
  N8: SW1.16, 7486_XOR1.XOR_1_-_IN_1, 7408_AND1.AND_1_-_IN_1
  N9: 7486_XOR1.XOR_2_-_OUT, 7486_XOR1.XOR_3_-_IN_2, 7408_AND1.AND_3_-_IN_2
  N10: 7486_XOR1.XOR_3_-_IN_1, 7408_AND1.AND_1_OUT, 7408_AND1.AND_3_-_IN_1
  N11: 7486_XOR1.XOR_4_-_OUT, 7486_XOR2.XOR_1_-_IN_1, 7408_AND2.AND_1_-_IN_1
  N12: 7408_AND1.AND_2_-_OUT, 7432.NAND_1_-_IN_1
  N13: 7408_AND1.AND_3_-_OUT, 7432.NAND_1_-_IN_2
  N14: 7408_AND1.AND_4_-_OUT, 7432.NAND_2_-_IN_1
  N15: 7432.NAND_1_OUT, 7486_XOR2.XOR_1_-_IN_2, 7408_AND2.AND_1_-_IN_2
  N16: 7432.NAND_2_-_IN_2, 7408_AND2.AND_1_OUT
  N17: 7432.NAND_2_-_OUT, 7486_XOR2.XOR_3_-_IN_2, 7408_AND2.AND_3_-_IN_2
  N18: 7432.NAND_3_-_IN_2, 7408_AND2.AND_3_-_OUT
  N19: 7432.NAND_3_-_IN_1, 7408_AND2.AND_2_-_OUT
  N20: 7486_XOR2.XOR_2_-_OUT, 7486_XOR2.XOR_3_-_IN_1, 7408_AND2.AND_3_-_IN_1

notes:
  S-1 OUT
  S-2 OUT
  S-3 OUT
  S-4 OUT
  C-4 OUT

custom parts:
  IC 7486 Quad XOR Gate: IC 7486 Quad 2-Input XOR Gate
  IC 7408 AND Gate: IC 7408 Quad 2-Input AND Gate
  7432 Quad OR Gate: IC 7432 Quad 2-Input OR Gate
