# Fritzing sketch Astable 555 Circuit (saved by Fritzing 0.9.1b)
breadboards: 1

parts:
  U1 = 555 Timer [package="DIP8 [THT]"]
  R1 = Resistor [tolerance=±5% resistance=470k package=THT]
  R2 = Resistor [tolerance=±5% resistance=1k package=THT]
  R3 = Resistor [tolerance=±5% resistance=1k package=THT]
  LED1 = LED - 5mm [color="Red (633nm)" package="5 mm [THT]"]
  C1 = Electrolytic Capacitor [capacitance=2.2µF package="100 mil [THT, electrolytic]"]
  Vcc = DC Power [voltage=6]

nets:
  N1: U1.Ground, LED1.cathode, C1.-, Vcc.V-
  N2: U1.Trigger, U1.Threshold, R1.Pin_1, C1.+
  N3: U1.Output, R3.Pin_0
  N4: U1.Reset, U1.Vcc_Supply_Voltage, R2.Pin_0, Vcc.V+
  N5: U1.Discharge, R1.Pin_0, R2.Pin_1
  N6: R3.Pin_1, LED1.anode
