# Fritzing sketch keypad number display (saved by Fritzing 0.9.1b)
breadboards: 1

parts:
  * = Pushbutton [package=THT]  # not connected
  1 = Pushbutton [package=THT]
  5 = Pushbutton [package=THT]
  7 = Pushbutton [package=THT]
  2 = Pushbutton [package=THT]
  4 = Pushbutton [package=THT]
  6 = Pushbutton [package=THT]
  3 = Pushbutton [package=THT]
  0 = Pushbutton [package=THT]  # not connected
  # = Pushbutton [package=THT]  # not connected
  9 = Pushbutton [package=THT]
  8 = Pushbutton [package=THT]
  IC1 = IC, DIP package, 16 pins [chip_label=IC]
  7_Segment1 = 7 Segment Display

nets:
  N1: 1.leg1, 5.leg1, 7.leg1, 2.leg1, 4.leg1, 6.leg1, 3.leg1, 9.leg1, 8.leg1, IC1.pin5, IC1.pin6, IC1.pin7, IC1.pin8
  N2: IC1.pin9, 7_Segment1.Segment_DP
  N3: IC1.pin10, 7_Segment1.Segment_G
  N4: IC1.pin11, 7_Segment1.Segment_F
  N5: IC1.pin12, 7_Segment1.Segment_E
  N6: IC1.pin13, 7_Segment1.Segment_D
  N7: IC1.pin14, 7_Segment1.Segment_C
  N8: IC1.pin15, 7_Segment1.Segment_B
  N9: IC1.pin16, 7_Segment1.Segment_A
